# Fritzing sketch wiring (saved by Fritzing 0.9.6b)
circuit board: 8.46667cm x 5.64444cm
breadboards: 1

parts:
  Raspberry_Pi_1 = Raspberry Pi 3 [part_number=RPI-3-V1.2]
  MPU9250_MPU-1 = SparkFun IMU Breakout - MPU-9250 [part_number=" SEN-13762"]
  S1 = Pushbutton [package="[SMD]"]
  LED1 = LED - 5mm [color="Green (555nm)" current=0.030 package="5 mm [THT]"]
  R1 = Resistor [tolerance=±5% power=0.25 resistance=330 package=THT]
  LED2 = LED - 5mm [color="Red (633nm)" current=0.030 package="5 mm [THT]"]
  R2 = Resistor [tolerance=±5% power=0.25 resistance=330 package=THT]

nets (from the schematic view):
  3V3: Raspberry_Pi_1.3v3, MPU9250_MPU-1.VDD
  N1: Raspberry_Pi_1.GPIO2, MPU9250_MPU-1.SDA/SDI
  N2: Raspberry_Pi_1.GPIO3, MPU9250_MPU-1.SCL/SCLK
  GND: Raspberry_Pi_1.GND, Raspberry_Pi_1.GIPO23, MPU9250_MPU-1.GND, LED1.cathode, LED2.cathode
  N3: Raspberry_Pi_1.GIPO7, R2.Pin_1
  N4: Raspberry_Pi_1.GIPO8, R1.Pin_1
  N5: S1.Pin_1, S1.Pin_2
  N6: S1.Pin_3, S1.Pin_4
  N7: LED2.anode, R2.Pin_0
